# Fritzing sketch Sketch (saved by Fritzing 0.9.3b)
breadboards: 1

parts:
  Componente1 = Arduino Nano (Rev3.0)
  Relay_5V1 = Keyes Relay [package=THT]

nets:
  N1: Componente1.GND, Relay_5V1.ground
  N2: Componente1.5V, Relay_5V1.power
  N3: Componente1.D13/SCK, Relay_5V1.signal

notes:
  + out - model
  S + -
  model

custom parts:
  Keyes Relay: The Keyes 5V relay module is suitable for SCM development, home appliance control. It uses a 5V~12V TIL control signal which can control DC / AC signal.
